// Logisim project clock.circ as structural Verilog: 1 circuit, main circuit main
module main (
);

  wire clock_1_out, j_k_ff_1_q, n7430_1_pin8, n7430_2_pin1, n7430_2_pin2, n7430_2_pin3, n7430_2_pin4,
       n7430_2_pin5, n7430_2_pin6, n7430_2_pin8, n7430_2_pin11, n7430_2_pin12, n74139_1_pin1, n74139_1_pin4,
       n74139_1_pin5, n74139_1_pin6, n74139_1_pin7, n74139_1_pin13, n74139_1_pin14, n74139_1_pin15,
       n74163_1_pin2, n74163_1_pin3, n74163_1_pin4, n74163_1_pin5, n74163_1_pin6, n74163_1_pin7,
       n74163_1_pin9, n74163_1_pin10, n74163_2_pin3, n74163_2_pin4, n74163_2_pin5, n74163_2_pin6,
       n74163_2_pin7, n74163_2_pin10, n74163_3_pin3, n74163_3_pin4, n74163_3_pin5, n74163_3_pin6,
       n74163_3_pin7, n74163_3_pin10, n74163_4_pin3, n74163_4_pin4, n74163_4_pin5, n74163_4_pin6,
       n74163_4_pin7, n74163_4_pin9, n74163_4_pin10, n74163_5_pin3, n74163_5_pin4, n74163_5_pin5,
       n74163_5_pin6, n74163_5_pin7, n74163_5_pin9, n74163_5_pin10, transistor_1_out, transistor_2_out,
       transistor_3_out, transistor_4_out, transistor_5_out, transistor_6_out, transistor_7_out,
       transistor_8_out, transistor_9_out, transistor_10_out, transistor_11_out, transistor_12_out,
       transistor_13_out, transistor_14_out, transistor_15_out, transistor_16_out, transistor_17_out,
       transistor_18_out, transistor_19_out, transistor_20_out, transistor_21_out, transistor_22_out,
       transistor_23_out, transistor_24_out, transistor_25_out, transistor_26_out, transistor_27_out,
       transistor_28_out;
  wire [7:0] rom_1_data;
  wire [12:0] n7430_1_pin2;

  _7430 #(.ShowInternalStructure("true")) u_7430_1 (
    .pin1(n7430_1_pin2[1]), .pin2(n7430_1_pin2[0]), .pin3(n7430_1_pin2[7]), .pin4(n7430_1_pin2[4]),
    .pin5(n7430_1_pin2[10]), .pin6(n7430_1_pin2[8]), .pin12(n7430_1_pin2[2]), .pin11(n7430_1_pin2[3]),
    .pin8(n7430_1_pin8));  // open: pin13, pin10, pin9
  _74163 #(.ShowInternalStructure("true")) u_74163_1 (
    .pin1(n7430_1_pin8), .pin2(n74163_1_pin2), .pin3(n74163_1_pin3), .pin4(n74163_1_pin4),
    .pin5(n74163_1_pin5), .pin6(n74163_1_pin6), .pin7(n74163_1_pin7), .pin14(n7430_1_pin2[8]),
    .pin13(n7430_1_pin2[9]), .pin12(n7430_1_pin2[10]), .pin10(n74163_1_pin10), .pin9(n74163_1_pin9));  // open: pin15, pin11
  _74163 #(.ShowInternalStructure("true")) u_74163_2 (
    .pin1(n7430_1_pin8), .pin2(n74163_1_pin2), .pin3(n74163_2_pin3), .pin4(n74163_2_pin4),
    .pin5(n74163_2_pin5), .pin6(n74163_2_pin6), .pin7(n74163_2_pin7), .pin15(n74163_1_pin10),
    .pin14(n7430_1_pin2[4]), .pin13(n7430_1_pin2[5]), .pin12(n7430_1_pin2[6]), .pin11(n7430_1_pin2[7]),
    .pin10(n74163_2_pin10), .pin9(n74163_1_pin9));
  _74163 #(.ShowInternalStructure("true")) u_74163_3 (
    .pin1(n7430_1_pin8), .pin2(n74163_1_pin2), .pin3(n74163_3_pin3), .pin4(n74163_3_pin4),
    .pin5(n74163_3_pin5), .pin6(n74163_3_pin6), .pin7(n74163_3_pin7), .pin15(n74163_2_pin10),
    .pin14(n7430_1_pin2[0]), .pin13(n7430_1_pin2[1]), .pin12(n7430_1_pin2[2]), .pin11(n7430_1_pin2[3]),
    .pin10(n74163_3_pin10), .pin9(n74163_1_pin9));
  ROM #(.addrWidth(13)) rom_1 (.addr(n7430_1_pin2), .data(rom_1_data));
  nand nand_1 (n74163_3_pin10, n7430_2_pin8, n7430_2_pin8);
  _7430 #(.ShowInternalStructure("true")) u_7430_2 (
    .pin1(n7430_2_pin1), .pin2(n7430_2_pin2), .pin3(n7430_2_pin3), .pin4(n7430_2_pin4), .pin5(n7430_2_pin5),
    .pin6(n7430_2_pin6), .pin12(n7430_2_pin12), .pin11(n7430_2_pin11), .pin8(n7430_2_pin8));  // open: pin13, pin10, pin9
  _74163 #(.ShowInternalStructure("true")) u_74163_4 (
    .pin1(n7430_2_pin8), .pin2(n74163_1_pin2), .pin3(n74163_4_pin3), .pin4(n74163_4_pin4),
    .pin5(n74163_4_pin5), .pin6(n74163_4_pin6), .pin7(n74163_4_pin7), .pin14(n7430_2_pin3),
    .pin13(n7430_2_pin2), .pin10(n74163_4_pin10), .pin9(n74163_4_pin9));  // open: pin15, pin12, pin11
  Transistor transistor_1 (.in(rom_1_data[0]), .out(transistor_1_out), .gate(n74139_1_pin7));
  Transistor transistor_2 (.in(rom_1_data[5]), .out(transistor_2_out), .gate(n74139_1_pin7));
  Transistor transistor_3 (.in(rom_1_data[6]), .out(transistor_3_out), .gate(n74139_1_pin7));
  Clock clock_1 (.out(clock_1_out));
  _74163 #(.ShowInternalStructure("true")) u_74163_5 (
    .pin1(n7430_2_pin8), .pin2(n74163_1_pin2), .pin3(n74163_5_pin3), .pin4(n74163_5_pin4),
    .pin5(n74163_5_pin5), .pin6(n74163_5_pin6), .pin7(n74163_5_pin7), .pin15(n74163_4_pin10),
    .pin14(n7430_2_pin1), .pin13(n7430_2_pin12), .pin11(n7430_2_pin11), .pin10(n74163_5_pin10),
    .pin9(n74163_5_pin9));  // open: pin12
  _7_Segment_Display u_7_segment_display_1 (
    .g(transistor_3_out), .f(transistor_2_out), .a(transistor_1_out), .b(transistor_7_out),
    .e(transistor_4_out), .d(transistor_5_out), .c(transistor_6_out), .dp(1'b0));
  Transistor transistor_4 (.in(rom_1_data[4]), .out(transistor_4_out), .gate(n74139_1_pin7));
  Transistor transistor_5 (.in(rom_1_data[3]), .out(transistor_5_out), .gate(n74139_1_pin7));
  Transistor transistor_6 (.in(rom_1_data[2]), .out(transistor_6_out), .gate(n74139_1_pin7));
  Transistor transistor_7 (.in(rom_1_data[1]), .out(transistor_7_out), .gate(n74139_1_pin7));
  J_K_Flip_Flop j_k_ff_1 (
    .J(1'b1), .K(1'b1), .clk(clock_1_out), .Q(j_k_ff_1_q), .Qn(n7430_1_pin2[11]));  // open: preset, reset
  _7_Segment_Display u_7_segment_display_2 (
    .g(transistor_10_out), .f(transistor_9_out), .a(transistor_8_out), .b(transistor_14_out),
    .e(transistor_11_out), .d(transistor_12_out), .c(transistor_13_out), .dp(1'b0));
  Transistor transistor_8 (.in(rom_1_data[0]), .out(transistor_8_out), .gate(n74139_1_pin7));
  Transistor transistor_9 (.in(rom_1_data[5]), .out(transistor_9_out), .gate(n74139_1_pin6));
  Transistor transistor_10 (.in(rom_1_data[6]), .out(transistor_10_out), .gate(n74139_1_pin6));
  Transistor transistor_11 (.in(rom_1_data[4]), .out(transistor_11_out), .gate(n74139_1_pin6));
  Transistor transistor_12 (.in(rom_1_data[3]), .out(transistor_12_out), .gate(n74139_1_pin6));
  Transistor transistor_13 (.in(rom_1_data[2]), .out(transistor_13_out), .gate(n74139_1_pin6));
  _74139 #(.ShowInternalStructure("true")) u_74139_1 (
    .pin1(n74139_1_pin1), .pin2(n7430_1_pin2[11]), .pin3(n7430_1_pin2[12]), .pin4(n74139_1_pin4),
    .pin5(n74139_1_pin5), .pin6(n74139_1_pin6), .pin7(n74139_1_pin7), .pin15(n74139_1_pin15),
    .pin14(n74139_1_pin14), .pin13(n74139_1_pin13));  // open: pin12, pin11, pin10, pin9
  J_K_Flip_Flop j_k_ff_2 (.J(1'b1), .K(1'b1), .clk(j_k_ff_1_q), .Qn(n7430_1_pin2[12]));  // open: Q, preset, reset
  Clock #(.highDuration(10), .lowDuration(10)) clock_2 (.out(n74163_1_pin2));
  Transistor transistor_14 (.in(rom_1_data[1]), .out(transistor_14_out), .gate(n74139_1_pin6));
  Transistor transistor_15 (.in(rom_1_data[0]), .out(transistor_15_out), .gate(n74139_1_pin6));
  Transistor transistor_16 (.in(rom_1_data[5]), .out(transistor_16_out), .gate(n74139_1_pin5));
  Transistor transistor_17 (.in(rom_1_data[6]), .out(transistor_17_out), .gate(n74139_1_pin5));
  _7_Segment_Display u_7_segment_display_3 (
    .g(transistor_17_out), .f(transistor_16_out), .a(transistor_15_out), .b(transistor_21_out),
    .e(transistor_18_out), .d(transistor_19_out), .c(transistor_20_out), .dp(1'b0));
  Transistor transistor_18 (.in(rom_1_data[4]), .out(transistor_18_out), .gate(n74139_1_pin5));
  Transistor transistor_19 (.in(rom_1_data[3]), .out(transistor_19_out), .gate(n74139_1_pin5));
  Transistor transistor_20 (.in(rom_1_data[2]), .out(transistor_20_out), .gate(n74139_1_pin5));
  Transistor transistor_21 (.in(rom_1_data[1]), .out(transistor_21_out), .gate(n74139_1_pin5));
  _7_Segment_Display u_7_segment_display_4 (
    .g(transistor_24_out), .f(transistor_23_out), .a(transistor_22_out), .b(transistor_28_out),
    .e(transistor_25_out), .d(transistor_26_out), .c(transistor_27_out), .dp(1'b0));
  Transistor transistor_22 (.in(rom_1_data[0]), .out(transistor_22_out), .gate(n74139_1_pin5));
  Transistor transistor_23 (.in(rom_1_data[5]), .out(transistor_23_out), .gate(n74139_1_pin4));
  Transistor transistor_24 (.in(rom_1_data[6]), .out(transistor_24_out), .gate(n74139_1_pin4));
  Transistor transistor_25 (.in(rom_1_data[4]), .out(transistor_25_out), .gate(n74139_1_pin4));
  Transistor transistor_26 (.in(rom_1_data[3]), .out(transistor_26_out), .gate(n74139_1_pin4));
  Transistor transistor_27 (.in(rom_1_data[2]), .out(transistor_27_out), .gate(n74139_1_pin4));
  Transistor transistor_28 (.in(rom_1_data[1]), .out(transistor_28_out), .gate(n74139_1_pin4));
  // also tied to GND on the sheet: {n74163_1_pin3, n74163_1_pin4, n74163_1_pin5, n74163_1_pin6, n74163_2_pin3, n74163_2_pin4, n74163_2_pin5, n74163_2_pin6, n74163_3_pin3, n74163_3_pin4, n74163_3_pin5, n74163_3_pin6, n74163_4_pin3, n74163_4_pin4, n74163_4_pin5, n74163_4_pin6, n74163_5_pin3, n74163_5_pin4, n74163_5_pin5, n74163_5_pin6, n74139_1_pin1, n74139_1_pin14, n74139_1_pin13}
  // also tied to VCC on the sheet: {n74163_1_pin7, n74163_2_pin7, n74163_3_pin7, n74163_1_pin9, n7430_2_pin4, n7430_2_pin5, n7430_2_pin6, n74163_4_pin7, n74163_4_pin9, n74163_5_pin10, n74163_5_pin7, n74163_5_pin9, n74139_1_pin15}

  // Notes on the sheet:
  //   contents of rom_1 (hex, n*v repeats v):
  //   3f 6 5b 4f 66 6d 7d 7 7f 6f 3f 6 5b 4f 66 6d 7d 7 7f 6f 3f 6 5b 4f 66 6d 7d 7 7f 6f 3f 6 5b 4f 66 6d
  //   7d 7 7f 6f 3f 6 5b 4f 66 6d 7d 7 7f 6f 3f 6 5b 4f 66 6d 7d 7 7f 6f 3f 6 5b 4f 66 6d 7d 7 7f 6f 3f 6
  //   5b 4f 66 6d 7d 7 7f 6f 3f 6 5b 4f 66 6d 7d 7 7f 6f 3f 6 5b 4f 66 6d 7d 7 7f 6f 3f 6 5b 4f 66 6d 7d 7
  //   7f 6f 3f 6 5b 4f 66 6d 7d 7 7f 6f 3f 6 5b 4f 66 6d 7d 7 7f 6f 3f 6 5b 4f 66 6d 7d 7 7f 6f 3f 6 5b 4f
  //   66 6d 7d 7 7f 6f 3f 6 5b 4f 66 6d 7d 7 7f 6f 3f 6 5b 4f 66 6d 7d 7 7f 6f 3f 6 5b 4f 66 6d 7d 7 7f 6f
  //   3f 6 5b 4f 66 6d 7d 7 7f 6f 3f 6 5b 4f 66 6d 7d 7 7f 6f 3f 6 5b 4f 66 6d 7d 7 7f 6f 3f 6 5b 4f 66 6d
  //   7d 7 7f 6f 3f 6 5b 4f 66 6d 7d 7 7f 6f 3f 6 5b 4f 66 6d 7d 7 7f 6f 3f 6 5b 4f 66 6d 7d 7 7f 6f 3f 6
  //   5b 4f 66 6d 7d 7 7f 6f 3f 6 5b 4f 66 6d 7d 7 7f 6f 3f 6 5b 4f 66 6d 7d 7 7f 6f 3f 6 5b 4f 66 6d 7d 7
  //   7f 6f 3f 6 5b 4f 66 6d 7d 7 7f 6f 3f 6 5b 4f 66 6d 7d 7 7f 6f 3f 6 5b 4f 66 6d 7d 7 7f 6f 3f 6 5b 4f
  //   66 6d 7d 7 7f 6f 3f 6 5b 4f 66 6d 7d 7 7f 6f 3f 6 5b 4f 66 6d 7d 7 7f 6f 3f 6 5b 4f 66 6d 7d 7 7f 6f
  //   3f 6 5b 4f 66 6d 7d 7 7f 6f 3f 6 5b 4f 66 6d 7d 7 7f 6f 3f 6 5b 4f 66 6d 7d 7 7f 6f 3f 6 5b 4f 66 6d
  //   7d 7 7f 6f 3f 6 5b 4f 66 6d 7d 7 7f 6f 3f 6 5b 4f 66 6d 7d 7 7f 6f 3f 6 5b 4f 66 6d 7d 7 7f 6f 3f 6
  //   5b 4f 66 6d 7d 7 7f 6f 3f 6 5b 4f 66 6d 7d 7 7f 6f 3f 6 5b 4f 66 6d 7d 7 7f 6f 3f 6 5b 4f 66 6d 7d 7
  //   7f 6f 3f 6 5b 4f 66 6d 7d 7 7f 6f 3f 6 5b 4f 66 6d 7d 7 7f 6f 3f 6 5b 4f 66 6d 7d 7 7f 6f 3f 6 5b 4f
  //   66 6d 7d 7 7f 6f 3f 6 5b 4f 66 6d 7d 7 7f 6f 3f 6 5b 4f 66 6d 7d 7 7f 6f 3f 6 5b 4f 66 6d 7d 7 7f 6f
  //   3f 6 5b 4f 66 6d 7d 7 7f 6f 3f 6 5b 4f 66 6d 7d 7 7f 6f 3f 6 5b 4f 66 6d 7d 7 7f 6f 3f 6 5b 4f 66 6d
  //   7d 7 7f 6f 3f 6 5b 4f 66 6d 7d 7 7f 6f 3f 6 5b 4f 66 6d 7d 7 7f 6f 3f 6 5b 4f 66 6d 7d 7 7f 6f 3f 6
  //   5b 4f 66 6d 7d 7 7f 6f 3f 6 5b 4f 66 6d 7d 7 7f 6f 3f 6 5b 4f 66 6d 7d 7 7f 6f 3f 6 5b 4f 66 6d 7d 7
  //   7f 6f 3f 6 5b 4f 66 6d 7d 7 7f 6f 3f 6 5b 4f 66 6d 7d 7 7f 6f 3f 6 5b 4f 66 6d 7d 7 7f 6f 3f 6 5b 4f
  //   66 6d 7d 7 7f 6f 3f 6 5b 4f 66 6d 7d 7 7f 6f 3f 6 5b 4f 66 6d 7d 7 7f 6f 3f 6 5b 4f 66 6d 7d 7 7f 6f
  //   bf 86 db cf e6 ed fd 87 ff ef bf 86 db cf e6 ed fd 87 ff ef bf 86 db cf e6 ed fd 87 ff ef bf 86 db
  //   cf e6 ed fd 87 ff ef bf 86 db cf e6 ed fd 87 ff ef bf 86 db cf e6 ed fd 87 ff ef bf 86 db cf e6 ed
  //   fd 87 ff ef bf 86 db cf e6 ed fd 87 ff ef bf 86 db cf e6 ed fd 87 ff ef bf 86 db cf e6 ed fd 87 ff
  //   ef bf 86 db cf e6 ed fd 87 ff ef bf 86 db cf e6 ed fd 87 ff ef bf 86 db cf e6 ed fd 87 ff ef bf 86
  //   db cf e6 ed fd 87 ff ef bf 86 db cf e6 ed fd 87 ff ef bf 86 db cf e6 ed fd 87 ff ef bf 86 db cf e6
  //   ed fd 87 ff ef bf 86 db cf e6 ed fd 87 ff ef bf 86 db cf e6 ed fd 87 ff ef bf 86 db cf e6 ed fd 87
  //   ff ef bf 86 db cf e6 ed fd 87 ff ef bf 86 db cf e6 ed fd 87 ff ef bf 86 db cf e6 ed fd 87 ff ef bf
  //   86 db cf e6 ed fd 87 ff ef bf 86 db cf e6 ed fd 87 ff ef bf 86 db cf e6 ed fd 87 ff ef bf 86 db cf
  //   e6 ed fd 87 ff ef bf 86 db cf e6 ed fd 87 ff ef bf 86 db cf e6 ed fd 87 ff ef bf 86 db cf e6 ed fd
  //   87 ff ef bf 86 db cf e6 ed fd 87 ff ef bf 86 db cf e6 ed fd 87 ff ef bf 86 db cf e6 ed fd 87 ff ef
  //   bf 86 db cf e6 ed fd 87 ff ef bf 86 db cf e6 ed fd 87 ff ef bf 86 db cf e6 ed fd 87 ff ef bf 86 db
  //   cf e6 ed fd 87 ff ef bf 86 db cf e6 ed fd 87 ff ef bf 86 db cf e6 ed fd 87 ff ef bf 86 db cf e6 ed
  //   fd 87 ff ef bf 86 db cf e6 ed fd 87 ff ef bf 86 db cf e6 ed fd 87 ff ef bf 86 db cf e6 ed fd 87 ff
  //   ef bf 86 db cf e6 ed fd 87 ff ef bf 86 db cf e6 ed fd 87 ff ef bf 86 db cf e6 ed fd 87 ff ef bf 86
  //   db cf e6 ed fd 87 ff ef bf 86 db cf e6 ed fd 87 ff ef bf 86 db cf e6 ed fd 87 ff ef bf 86 db cf e6
  //   ed fd 87 ff ef bf 86 db cf e6 ed fd 87 ff ef bf 86 db cf e6 ed fd 87 ff ef bf 86 db cf e6 ed fd 87
  //   ff ef bf 86 db cf e6 ed fd 87 ff ef bf 86 db cf e6 ed fd 87 ff ef bf 86 db cf e6 ed fd 87 ff ef bf
  //   86 db cf e6 ed fd 87 ff ef bf 86 db cf e6 ed fd 87 ff ef bf 86 db cf e6 ed fd 87 ff ef bf 86 db cf
  //   e6 ed fd 87 ff ef bf 86 db cf e6 ed fd 87 ff ef bf 86 db cf e6 ed fd 87 ff ef bf 86 db cf e6 ed fd
  //   87 ff ef bf 86 db cf e6 ed fd 87 ff ef bf 86 db cf e6 ed fd 87 ff ef bf 86 db cf e6 ed fd 87 ff ef
  //   bf 8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
endmodule
